# Fritzing sketch PT2399_ケース内配線 (saved by Fritzing 0.9.2b)
perfboards: 1

parts:
  J1 = female pin header, 2 pins [form="♀ (female)"]
  J2 = female pin header, 3 pins [form="♀ (female)"]
  J3 = female pin header, 3 pins [form="♀ (female)"]
  J4 = female pin header, 3 pins [form="♀ (female)"]
  J5 = female pin header, 2 pins [form="♀ (female)"]
  J6 = female pin header, 2 pins [form="♀ (female)"]
  VCC1 = Battery block 9V
  R1 = Rotary Potentiometer (Small) [maximum_resistance=100kΩ package=THT]
  R2 = Rotary Potentiometer (Small) [maximum_resistance=100kΩ package=THT]
  R3 = Rotary Potentiometer (Small) [maximum_resistance=100kΩ package=THT]
  JP1 = RCA [package=rca_lock]
  JP2 = RCA [package=rca_lock]
  S1 = Toggle Switch [package=THT]

nets:
  N1: J1.pin1, JP1.PIN
  N2: J1.pin2, JP1.SHELL
  N3: J2.pin1, R1.leg2
  N4: J2.pin2, R1.wiper
  N5: J2.pin3, R1.leg1
  N6: J3.pin1, R2.leg2
  N7: J3.pin2, R2.wiper
  N8: J3.pin3, R2.leg1
  N9: J4.pin1, R3.leg2
  N10: J4.pin2, R3.wiper
  N11: J4.pin3, R3.leg1
  N12: J5.pin1, JP2.PIN
  N13: J5.pin2, JP2.SHELL
  N14: J6.pin1, VCC1.-
  N15: J6.pin2, S1.COM

notes:
  PT2399 Kit
